// Logisim project myComparator.circ as structural Verilog: 1 circuit, main circuit myComparator
module myComparator (
  input  [1:0] A,
  input  [1:0] B,
  output Eq,
  output LT
);


  // Notes on the sheet:
  //   Input
  //   DO NOT CROSS WIRES
  //   OVER THIS BOX
  //   Note
  //   Please, do not modify/change/replace the input and output pins
  //   Comparator: Eq and LT
  //   DO NOT CROSS WIRES
  //   OVER THIS BOX
  //   Output
  //   DO NOT CROSS WIRES
  //   OVER THIS BOX
endmodule
