// Logisim project rotr.circ as structural Verilog: 1 circuit, main circuit rotr
module rotr (
  input  [15:0] A,
  input  [3:0] B,
  output [15:0] C
);


  // Notes on the sheet:
  //   Input
  //   DO NOT CROSS WIRES
  //   OVER THIS BOX
  //   Note
  //   Please, do not modify/change/replace the input and output pins
  //   Shamt
  //   OVER THIS BOX
  //   Rotate Right
  //   DO NOT CROSS WIRES
  //   DO NOT CROSS WIRES
  //   OVER THIS BOX
  //   Output
  //   DO NOT CROSS WIRES
  //   OVER THIS BOX
endmodule
