// Logisim project splitters.circ as structural Verilog: 1 circuit, main circuit main
module main (
  input  [7:0] In,
  output Out1,
  output [7:0] Out2
);


  // Notes on the sheet:
  //   Input
  //   DO NOT CROSS WIRES
  //   OVER THIS BOX
  //   Note
  //   Please, do not modify/change/replace the input and output pins
  //   Splitters
  //   DO NOT CROSS WIRES
  //   OVER THIS BOX
  //   Outputs
  //   DO NOT CROSS WIRES
  //   OVER THIS BOX
endmodule
