// Logisim project comparator_test.circ as structural Verilog: 1 circuit, main circuit main
module main (
  output [1:0] out_1,
  output [1:0] out_2,
  output out_3,
  output out_4,
  output halt
);

  wire clk;
  wire [3:0] adder_1_out;

  Register #(.width(4)) register_1 (.D(adder_1_out), .Q({out_2, out_1}), .clk(clk));  // open: en, clr
  Clock clock_1 (.out(clk));
  Adder #(.width(4)) adder_1 (.a(4'b0001), .b({out_2, out_1}), .out(adder_1_out));  // open: cin, cout
  Comparator #(.width(4), .mode("unsigned")) comparator_1 (.a(4'b1111), .b({out_2, out_1}), .eq(halt));  // open: gt, lt
  myComparator mycomparator_1 (.A(out_1), .B(out_2), .Eq(out_3), .LT(out_4));

  // Other names for the same wires on the sheet: A[1:0] = out_1; cnt[3:0] = {out_2, out_1}; B[1:0] = out_2;
  //   Eq = out_3; LT = out_4

  // Notes on the sheet:
  //   Counter
  //   Halt signal
  //   Output
  //   Note
  //   Please, do not modify this file
endmodule
