// Logisim project ex1.circ as structural Verilog: 1 circuit, main circuit main
module main (
  output [7:0] out_1,
  output out_2,
  output [7:0] out_3,
  output halt
);

  wire clock_1_out;
  wire [7:0] adder_1_out;

  Register register_1 (.D(adder_1_out), .Q(out_1), .clk(clock_1_out));  // open: en, clr
  Clock clock_1 (.out(clock_1_out));
  Comparator #(.mode("unsigned")) comparator_1 (.a({8{1'b1}}), .b(out_1), .eq(halt));  // open: gt, lt
  Adder adder_1 (.a(8'h1), .b(out_1), .out(adder_1_out));  // open: cin, cout
  splitters_main main_1 (.In(out_1), .Out1(out_2), .Out2(out_3));

  // Other names for the same wires on the sheet: In[7:0] = out_1; Out1 = out_2; Out2[7:0] = out_3

  // Notes on the sheet:
  //   Counter
  //   Halt signal
  //   Note
  //   Please, do not modify this file
endmodule
