// Logisim project ex2.circ as structural Verilog: 1 circuit, main circuit main
module main (
  output halt,
  output [7:0] out_2,
  output [15:0] out_3
);

  wire clk;
  wire [3:0] random_2_out;
  wire [7:0] adder_1_out;
  wire [15:0] random_1_out;

  Register register_1 (.D(adder_1_out), .Q(out_2), .clk(clk));  // open: en, clr
  Clock clock_1 (.out(clk));
  Adder adder_1 (.a(8'h1), .b(out_2), .out(adder_1_out));  // open: cin, cout
  Comparator #(.mode("unsigned")) comparator_1 (.a({8{1'b1}}), .b(out_2), .eq(halt));  // open: gt, lt
  Random #(.width(16), .seed(2)) random_1 (.clk(clk), .out(random_1_out));  // open: next, clr
  rotr rotr_1 (.A(random_1_out), .C(out_3), .B(random_2_out));
  Random #(.width(4), .seed(1)) random_2 (.clk(clk), .out(random_2_out));  // open: next, clr

  // Other names for the same wires on the sheet: cnt[7:0] = out_2; Out[15:0] = out_3

  // Notes on the sheet:
  //   Counter
  //   Halt signal
  //   Output
  //   Note
  //   Please, do not modify this file
endmodule
