// Logisim project ex3.circ as structural Verilog: 1 circuit, main circuit main
module main (
  output [7:0] out_1,
  output [31:0] out_2,
  output halt
);

  wire clk;
  wire [2:0] Control;
  wire [7:0] adder_1_out;
  wire [31:0] A, B;

  Register register_1 (.D(adder_1_out), .Q(out_1), .clk(clk));  // open: en, clr
  Clock clock_1 (.out(clk));
  Adder adder_1 (.a(8'h1), .b(out_1), .out(adder_1_out));  // open: cin, cout
  Comparator #(.mode("unsigned")) comparator_1 (.a({8{1'b1}}), .b(out_1), .eq(halt));  // open: gt, lt
  Random #(.width(32), .seed(1)) random_1 (.clk(clk), .out(A));  // open: next, clr
  Random #(.width(32), .seed(2)) random_2 (.clk(clk), .out(B));  // open: next, clr
  Random #(.width(3), .seed(3)) random_3 (.clk(clk), .out(Control));  // open: next, clr
  ALU alu_1 (.ALU_Source_1(A), .ALU_Source_2(A), .ALU_Result(out_2), .ALU_Control(Control));

  // Other names for the same wires on the sheet: cnt[7:0] = out_1; Out[31:0] = out_2

  // Notes on the sheet:
  //   Counter
  //   Halt signal
  //   Note
  //   Please, do not modify this file
endmodule
